// Logisim project RISCV.circ as structural Verilog: 8 circuits, main circuit RISCV32
module RISCV32 (
);

  wire and_1_out, and_2_out, and_3_out, and_4_out, clock_1_out, comparator_black_box_1_p4, nopcheck_1_nop,
       not_1_out, not_2_out, not_3_out, not_4_out, opsplitter_1_det_imm, opsplitter_1_load,
       opsplitter_1_loadbyte, opsplitter_1_lui, opsplitter_1_selofsel, opsplitter_1_slt, opsplitter_1_store,
       or_2_out, registerfile_1_p2, registerfile_1_p6;
  wire [3:0] multiplexer_5_out, nopcheck_1_sel, opsplitter_1_op, opsplitter_1_sel;
  wire [4:0] alu_1_p4, opsplitter_1_rd, opsplitter_1_rs1, opsplitter_1_rs2;
  wire [19:0] nopcheck_1_addy;
  wire [31:0] add4_1_o, alu_1_p2, alu_1_p5, bit_extender_2_out, comparator_black_box_1_p2, immgen_1_o,
       multiplexer_3_out, multiplexer_4_out, multiplexer_6_out, ram_1_p7, register_1_q, registerfile_1_p1,
       registerfile_1_p7, risc_vprogramrom_1_p2, split_1_o;

  Register #(.width(32)) register_1 (.D(add4_1_o), .clk(clock_1_out), .Q(register_1_q));  // open: en, clr
  Clock clock_1 (.out(clock_1_out));
  Add4 add4_1 (.I(register_1_q), .O(add4_1_o));
  // RISC_VProgramROM risc_vprogramrom_1: pin names not known; wires that end beside it: register_1_q, risc_vprogramrom_1_p2, clock_1_out
  OpSplitter opsplitter_1 (
    .in_1(risc_vprogramrom_1_p2), .rs2(opsplitter_1_rs2), .rs1(opsplitter_1_rs1), .Op(opsplitter_1_op),
    .rd(opsplitter_1_rd), .Det_imm(opsplitter_1_det_imm), .SLT(opsplitter_1_slt), .LUI(opsplitter_1_lui),
    .Store(opsplitter_1_store), .Sel(opsplitter_1_sel), .SelOfSel(opsplitter_1_selofsel),
    .Load(opsplitter_1_load), .LoadByte(opsplitter_1_loadbyte));
  ImmGen immgen_1 (.I(risc_vprogramrom_1_p2), .O(immgen_1_o));
  // RegisterFile registerfile_1: pin names not known; wires that end beside it: registerfile_1_p1, registerfile_1_p2, opsplitter_1_rd, opsplitter_1_rs1, opsplitter_1_rs2, registerfile_1_p6, registerfile_1_p7
  // ALU alu_1: pin names not known; wires that end beside it: registerfile_1_p6, alu_1_p2, opsplitter_1_op, alu_1_p4, alu_1_p5
  Multiplexer #(.width(32), .enable("false")) multiplexer_1 (
    .in0(registerfile_1_p7), .in1(immgen_1_o), .out(alu_1_p2), .sel(opsplitter_1_det_imm));
  Bit_Extender #(.in_width(32), .out_width(5)) bit_extender_1 (.in(registerfile_1_p7), .out(alu_1_p4));
  not not_1 (not_1_out, opsplitter_1_store);
  not not_2 (not_2_out, opsplitter_1_load);
  not not_3 (not_3_out, opsplitter_1_store);
  not not_4 (not_4_out, nopcheck_1_nop);
  // Comparator_Black_Box comparator_black_box_1: pin names not known; wires that end beside it: registerfile_1_p6, comparator_black_box_1_p2, opsplitter_1_slt, comparator_black_box_1_p4
  Multiplexer #(.width(32), .enable("false")) multiplexer_2 (
    .in0(registerfile_1_p7), .in1(immgen_1_o), .out(comparator_black_box_1_p2), .sel(opsplitter_1_det_imm));
  and and_1 (and_1_out, not_1_out, not_2_out);
  and and_2 (and_2_out, not_3_out, not_4_out);
  assign bit_extender_2_out = {{31{1'b0}}, comparator_black_box_1_p4};  // Bit_Extender bit_extender_2
  or or_1 (registerfile_1_p2, and_1_out, and_2_out);
  nopCheck nopcheck_1 (
    .I(alu_1_p5), .addy(nopcheck_1_addy), .nop(nopcheck_1_nop), .Sel(nopcheck_1_sel));  // open: nopVal
  Multiplexer #(.width(32), .enable("false")) multiplexer_3 (
    .in0(alu_1_p5), .in1(bit_extender_2_out), .out(multiplexer_3_out), .sel(opsplitter_1_slt));
  Multiplexer #(.width(32), .enable("false")) multiplexer_4 (
    .in0(multiplexer_3_out), .in1(immgen_1_o), .out(multiplexer_4_out), .sel(opsplitter_1_lui));
  Multiplexer #(.width(4), .enable("false")) multiplexer_5 (
    .in0(nopcheck_1_sel), .in1(opsplitter_1_sel), .out(multiplexer_5_out), .sel(opsplitter_1_selofsel));
  and and_3 (and_3_out, ~nopcheck_1_nop, opsplitter_1_store);  // AND_Gate
  and and_4 (and_4_out, ~nopcheck_1_nop, opsplitter_1_load);  // AND_Gate
  // RAM ram_1: pin names not known; wires that end beside it: nopcheck_1_addy, registerfile_1_p7, and_3_out, multiplexer_5_out, clock_1_out, and_4_out, ram_1_p7
  or or_2 (or_2_out, opsplitter_1_load, opsplitter_1_store);
  Multiplexer #(.width(32), .enable("false")) multiplexer_6 (
    .in0(ram_1_p7), .in1(split_1_o), .out(multiplexer_6_out), .sel(opsplitter_1_loadbyte));
  split split_1 (.I(ram_1_p7), .Sel(multiplexer_5_out), .O(split_1_o));
  Multiplexer #(.width(32), .enable("false")) multiplexer_7 (
    .in0(multiplexer_4_out), .in1(multiplexer_6_out), .out(registerfile_1_p1), .sel(or_2_out));

  // Notes on the sheet:
  //   contents of risc_vprogramrom_1 (hex, n*v repeats v):
  //   lui t0, 0x12345 addi t0, t0, 0x678 sw t0, 0(x0)  lui t0, 0x13f44 addi t0, t0, 0x64c sw t0, 4(x0)
  //   #TODO 1 #reverse word at memaddr 0 with bitmasks, store in t0 lw t0, 0(x0) lui x30, 0xff000 and x20,
  //   x30, x5 lui x30, 0x00ff0 and x21, x30, x5 lui x30, 0x00010 addi x30, x30, 0xf00 and x22, x30, x5 lui
  //   x30, 0x00000 addi x30, x30, 0x0ff and x23, x30, x5 addi x30, x0, 24 srl x20, x20,  x30  addi x30,
  //   x0, 8 srl x21, x21,  x30  addi x30, x0, 8 sll x22, x22,  x30  addi x30, x0, 24 sll x23, x23,  x30
  //   add x19, x23, x22 add x19, x19, x21 add x19, x19, x20 sw x19, 0(x0) lw t0, 0(x0)   #TODO 2 #reverse
  //   word at memaddr 4 with lb/sb, store in t1 lb x23, 4(x0) lb x24, 5(x0) lb x25, 6(x0) lb x26, 7(x0)
  //   sb x26, 4(x0) addi x27, x0, 8  sll x25, x25, x27 addi x27, x0, 16  sll x24, x24, x27 addi x27, x0,
  //   24  sll x23, x23, x27 sb x25, 5(x0) sb x24, 6(x0) sb x23, 7(x0) lw t1, 4(x0)   #TODO 3 #xor both
  //   reversed words, store in t2 xor t2, t0, t1
  //   WE
endmodule

module Add4 (
  input  [31:0] I,
  output [31:0] O
);

  // Incrementer #(.width(30)) incrementer_1: pin names not known; wires that end beside it: I[31:2], O[31:2]

  assign O[1:0] = I[1:0];
endmodule

module ImmGen (
  input  [31:0] I,
  output [31:0] O
);

  wire and_1_out, and_2_out, and_3_out, and_4_out, or_1_out;
  wire [31:0] bit_extender_1_out, bit_extender_2_out, bit_extender_3_out, multiplexer_1_out,
       multiplexer_2_out;

  and and_1 (and_1_out, I[0], I[1], ~I[2], ~I[3], I[4], ~I[5], ~I[6]);  // AND_Gate
  and and_2 (and_2_out, I[0], I[1], I[2], ~I[3], I[4], I[5], ~I[6]);  // AND_Gate
  and and_3 (and_3_out, I[0], I[1], ~I[2], ~I[3], ~I[4], I[5], ~I[6]);  // AND_Gate
  and and_4 (and_4_out, I[0], I[1], ~I[2], ~I[3], ~I[4], ~I[5], ~I[6]);  // AND_Gate
  assign bit_extender_1_out = {{12{1'b0}}, {I[12], I[13], I[14], I[15], I[16], I[17], I[18], I[19], I[20], I[21], I[22], I[23], I[24], I[25], I[26], I[27], I[28], I[29], I[30], I[31]}};  // Bit_Extender bit_extender_1
  assign bit_extender_2_out = {{20{I[31]}}, {I[31:25], I[11:7]}};  // Bit_Extender bit_extender_2
  assign bit_extender_3_out = {{20{I[31]}}, I[31:20]};  // Bit_Extender bit_extender_3
  Multiplexer #(.width(32), .enable("false")) multiplexer_1 (
    .in1(bit_extender_2_out), .out(multiplexer_1_out), .sel(and_3_out));  // open: in0
  Multiplexer #(.width(32), .enable("false")) multiplexer_2 (
    .in0(multiplexer_1_out),
    .in1({bit_extender_1_out[0], bit_extender_1_out[1], bit_extender_1_out[2], bit_extender_1_out[3], bit_extender_1_out[4], bit_extender_1_out[5], bit_extender_1_out[6], bit_extender_1_out[7], bit_extender_1_out[8], bit_extender_1_out[9], bit_extender_1_out[10], bit_extender_1_out[11], bit_extender_1_out[12], bit_extender_1_out[13], bit_extender_1_out[14], bit_extender_1_out[15], bit_extender_1_out[16], bit_extender_1_out[17], bit_extender_1_out[18], bit_extender_1_out[19], bit_extender_1_out[20], bit_extender_1_out[21], bit_extender_1_out[22], bit_extender_1_out[23], bit_extender_1_out[24], bit_extender_1_out[25], bit_extender_1_out[26], bit_extender_1_out[27], bit_extender_1_out[28], bit_extender_1_out[29], bit_extender_1_out[30], bit_extender_1_out[31]}),
    .out(multiplexer_2_out), .sel(and_2_out));
  Multiplexer #(.width(32), .enable("false")) multiplexer_3 (
    .in0(multiplexer_2_out), .in1(bit_extender_3_out), .out(O), .sel(or_1_out));
  or or_1 (or_1_out, and_1_out, and_4_out);

  // Notes on the sheet:
  //   LUI
  //   Store
  //   Load inst
  //   arithmetic w imm
endmodule

module OpSplitter (
  input  [31:0] in_1,
  output [4:0] rs2,
  output [4:0] rs1,
  output [3:0] Op,
  output [4:0] rd,
  output Det_imm,
  output SLT,
  output LUI,
  output Store,
  output [3:0] Sel,
  output SelOfSel,
  output Load,
  output LoadByte
);

  wire and_2_out, and_3_out, and_6_out, and_8_out, or_1_out;

  and and_1 (Store, ~in_1[6], in_1[5], ~in_1[4], ~in_1[3], ~in_1[2], in_1[1], in_1[0]);  // AND_Gate
  not not_1 (Det_imm, and_2_out);
  and and_2 (and_2_out, in_1[0], in_1[1], ~in_1[2], ~in_1[3], in_1[4], in_1[5], ~in_1[6]);  // AND_Gate
  and and_3 (and_3_out, in_1[0], in_1[1], ~in_1[2], ~in_1[3], in_1[4], ~in_1[5], ~in_1[6]);  // AND_Gate
  and and_4 (LUI, in_1[0], in_1[1], in_1[2], ~in_1[3], in_1[4], in_1[5], ~in_1[6]);  // AND_Gate
  and and_5 (Load, ~in_1[6], ~in_1[5], ~in_1[4], ~in_1[3], ~in_1[2], in_1[1], in_1[0]);  // AND_Gate
  SelComb selcomb_1 (.f3(in_1[12]), .f2(in_1[13]), .f1(in_1[14]), .out_4(Sel));
  and and_6 (and_6_out, ~in_1[14], in_1[13], ~in_1[12]);  // AND_Gate
  and and_7 (SelOfSel, Sel[0], Sel[1], Sel[3], Sel[2]);
  and and_8 (and_8_out, ~in_1[14], ~in_1[13], ~in_1[12]);  // AND_Gate
  OpTrans optrans_1 (
    .OpCode1(in_1[5]), .OpCode0(in_1[4]), .Funct3_2(in_1[14]), .Funct3_1(in_1[13]), .Funct3_0(in_1[12]),
    .Funct7_5(in_1[30]), .O3(Op[3]), .O2(Op[2]), .O1(Op[1]), .O0(Op[0]));
  and and_9 (LoadByte, and_8_out, Load);
  or or_1 (or_1_out, and_2_out, and_3_out);
  and and_10 (SLT, and_6_out, or_1_out);

  assign rd = in_1[11:7];
  assign rs1 = in_1[19:15];
  assign rs2 = in_1[24:20];
endmodule

module SelComb (
  input  f3,
  input  f2,
  input  f1,
  output [3:0] out_4
);

  or or_1 (out_4[0], f1, ~f1);  // OR_Gate
  or or_2 (out_4[3], f2, f3);

  assign out_4[2:1] = {2{f2}};
endmodule

module nopCheck (
  input  [31:0] I,
  output [19:0] addy,
  output nop,
  output [31:0] nopVal,
  output [3:0] Sel
);

  wire not_1_out, not_2_out, not_3_out, not_4_out;

  or or_1 (nop, I[22], I[23], I[24], I[25], I[26], I[28], I[29], I[30], I[31], I[27]);
  assign nopVal = {{31{nop}}, nop};  // Bit_Extender bit_extender_1
  and and_1 (Sel[3], I[1], I[0]);
  and and_2 (Sel[2], I[1], not_1_out);
  not not_1 (not_1_out, I[0]);
  not not_2 (not_2_out, I[1]);
  and and_3 (Sel[1], not_2_out, I[0]);
  not not_3 (not_3_out, I[1]);
  and and_4 (Sel[0], not_3_out, not_4_out);
  not not_4 (not_4_out, I[0]);

  assign addy = I[21:2];
endmodule

module OpTrans (
  input  OpCode1,
  input  OpCode0,
  input  Funct3_2,
  input  Funct3_1,
  input  Funct3_0,
  input  Funct7_5,
  output O3,
  output O2,
  output O1,
  output O0
);

  wire and_1_out, and_3_out, and_4_out, and_5_out, not_1_out, not_2_out;

  not not_1 (not_1_out, Funct3_0);
  not not_2 (not_2_out, Funct3_0);
  and and_1 (and_1_out, Funct3_2, Funct3_1);
  and and_2 (O0, Funct3_2, Funct3_0);
  and and_3 (and_3_out, Funct3_2, not_1_out);
  and and_4 (and_4_out, Funct3_2, Funct3_1);
  and and_5 (and_5_out, OpCode1, OpCode0, not_2_out, Funct7_5);
  or or_1 (O1, Funct3_0, and_1_out);
  or or_2 (O3, and_3_out, and_4_out);
  or or_3 (O2, Funct3_2, and_5_out);
endmodule

module split (
  input  [31:0] I,
  input  [3:0] Sel,
  output [31:0] O
);

  wire [7:0] multiplexer_1_out, multiplexer_2_out, multiplexer_3_out;

  Multiplexer #(.width(8), .enable("false")) multiplexer_1 (
    .in0(I[31:24]), .in1(I[23:16]), .out(multiplexer_1_out), .sel(Sel[2]));
  Multiplexer #(.width(8), .enable("false")) multiplexer_2 (
    .in0(multiplexer_1_out), .in1(I[15:8]), .out(multiplexer_2_out), .sel(Sel[1]));
  Multiplexer #(.width(8), .enable("false")) multiplexer_3 (
    .in0(multiplexer_2_out), .in1(I[7:0]), .out(multiplexer_3_out), .sel(Sel[0]));
  assign O = {{24{multiplexer_3_out[7]}}, multiplexer_3_out};  // Bit_Extender bit_extender_1
endmodule
